# Fritzing sketch Version 2.0 (saved by Fritzing 0.9.5d)
stripboards: 1

parts:
  Pico = Raspberry Pi Pico H
  Connector_24V_Power = Camdenboss CTB0158-2 [part_number=CTB0158-2 package=THT]
  Connector_Hall-Sensor = Camdenboss CTB0158-3 [part_number=CTB0158-3 package=THT]
  Connector_0-10V_PWM = Camdenboss CTB0158-2 [part_number=CTB0158-2 package=THT]
  Converter_24V_to_5V = RioRand LM2596
  Converter_24V_to_3_3V = RioRand LM2596
  PWM_to_0-10V_Converter = pwm to voltage converter module
  Rotary_Encoder = KY-040 Rotary encoder [package=THT]
  I2C-Display = LCD1602-I2C

nets:
  N1: Pico.VSYS, Converter_24V_to_5V.Pin_3
  N2: Pico.GP21, I2C-Display.SCL
  N3: Pico.GP20, I2C-Display.SDA
  N4: Pico.GP16, PWM_to_0-10V_Converter.Pin_5
  GND: Pico.GND, Connector_24V_Power.pin2, Connector_Hall-Sensor.pin3, Connector_0-10V_PWM.pin2, Converter_24V_to_5V.Pin_2, Converter_24V_to_3_3V.Pin_2, PWM_to_0-10V_Converter.Pin_6, PWM_to_0-10V_Converter.Pin_8, PWM_to_0-10V_Converter.Pin_9, Rotary_Encoder.GND, I2C-Display.GND
  N5: Pico.GP14, Connector_Hall-Sensor.pin2
  N6: Pico.GP4, Rotary_Encoder.SW
  N7: Pico.GP3, Rotary_Encoder.DT
  N8: Pico.GP2, Rotary_Encoder.CLK
  N9: Connector_24V_Power.pin1, Converter_24V_to_5V.Pin_1, Converter_24V_to_3_3V.Pin_1, PWM_to_0-10V_Converter.Pin_10
  VCC: Connector_Hall-Sensor.pin1, Converter_24V_to_3_3V.Pin_3, Rotary_Encoder.Vcc, I2C-Display.VCC
  N10: Connector_0-10V_PWM.pin1, PWM_to_0-10V_Converter.Pin_7

custom parts:
  Raspberry Pi Pico H: Raspberry Pi Pico H. Based around the RP2040 microcontroller the Pico H is a low cost microcontroller device bringing Raspberry Pi quality, cost, and easy of use to the microcontroller space.
  pwm to voltage converter module: The PWM transfer voltage module LC-LM358-PWM2V converts the PWM digital signals into 0 to 10V analog signals.
  KY-040 Rotary encoder: KY-040 Rotary Encoder with switch on breakout borad from AZ Delivery
  LCD1602-I2C: A standard character display, usually with 2x16 characters. Comes in many colors with LCM1602 IIC attached.
